# Fritzing sketch sketch (saved by Fritzing 0.9.4)
perfboards: 1

parts:
  WeMos_D1_Mini1_ftw = WeMos D1 Mini
  Part1 = PowerBoost 500 Charger
  R1_for_voltage_divider = Resistor [tolerance=±5% resistance=10k package="1206 [SMD]"]
  R2_for_voltage_divider = Resistor [tolerance=±5% resistance=33k package="1206 [SMD]"]
  Battery_Connector = female pin header, 2 pins [form="♀ (female)"]
  LED_Matrix_Connector = female pin header, 5 pins [form="♀ (female)"]
  Current_Limiting_Resistor_for_LED_Matrix = Resistor [tolerance=±5% resistance=10 package=THT]
  RST_jumper = male pin header, 2 pins [form="♂ (male)"]
  Power_Switch = female pin header, 2 pins [form="♀ (female)"]

nets:
  N1: WeMos_D1_Mini1_ftw.5V, Part1.5.0V
  N2: WeMos_D1_Mini1_ftw.D0, RST_jumper.pin1
  N3: WeMos_D1_Mini1_ftw.D5, LED_Matrix_Connector.pin3
  N4: WeMos_D1_Mini1_ftw.D7, LED_Matrix_Connector.pin4
  N5: WeMos_D1_Mini1_ftw.D8, LED_Matrix_Connector.pin5
  N6: WeMos_D1_Mini1_ftw.G, Part1.GND, R2_for_voltage_divider.Pin_0, Battery_Connector.pin1, Power_Switch.pin2
  N7: WeMos_D1_Mini1_ftw.RST, RST_jumper.pin2
  N8: Part1.VBAT_OUT, R1_for_voltage_divider.Pin_0, Battery_Connector.pin2
  N9: Part1.ENABLE, Power_Switch.pin1
  N10: LED_Matrix_Connector.pin2, Current_Limiting_Resistor_for_LED_Matrix.Pin_0
